# Fritzing sketch _1._Led_Yakma_Sondurme (saved by Fritzing 0.9.3b)
breadboards: 1

parts:
  Parça1 = Arduino Uno (Rev3)
  LED1 = LED - 5mm [color="Red (633nm)" package="5 mm [THT]"]
  R1 = Resistor [tolerance=±5% resistance=220 package=THT]

nets:
  N1: Parça1.D3_PWM, R1.Pin_0
  N2: Parça1.GND, LED1.cathode
  N3: LED1.anode, R1.Pin_1
